// Logisim project Cache_2.circ as structural Verilog: 11 circuits, main circuit implementation
module implementation (
  input  [9:0] CpuAddressIn,
  input  CpuReadIn,
  input  CpuWriteIn,
  input  [7:0] CpuWriteValueIn,
  input  [31:0] LineFromMemIn,
  input  ClkIn,
  output ReadyOut,
  output DidContainOut,
  output [7:0] ByteReadOut,
  output [7:0] MemAddressOut,
  output MemReadOut,
  output MemWriteOut,
  output [31:0] Line2MemOut
);

  wire CachReadsFromMem1, CachReadsFromMem2, CheckingIfCacheHasValue, counter_1_q, CpuWrite1, CpuWrite2,
       CpuWritesToCache, InternalContains, isDirty, OldestWayDirtyBit1, OldestWayDirtyBit2, PowerOn,
       PowerOnInternal, SetContains1, SetContains2, UpdateAges, UpdateAges1, UpdateAges2;
  wire [1:0] offset_bits;
  wire [3:0] nextstatefsm_1_nextstate, register_2_q;
  wire [6:0] InternalOldestTagToMem, OldestTagSet1, OldestTagSet2, OldestTagToMem;
  wire [7:0] ByteReadSet1, ByteReadSet2;
  wire [9:3] SavedCpuAddress;
  wire [31:0] InternalOldestWayToMem, OldestWaySet1, OldestWaySet2;

  Register #(.width(10)) register_1 (
    .D(CpuAddressIn), .en(ReadyOut), .clk(ClkIn), .Q({SavedCpuAddress, MemAddressOut[0], offset_bits}));  // open: clr
  Demultiplexer #(.enable("false")) demultiplexer_1 (
    .out0(CachReadsFromMem1), .out1(CachReadsFromMem2), .in(MemReadOut), .sel(MemAddressOut[0]));
  Demultiplexer #(.enable("false")) demultiplexer_2 (
    .out0(CpuWrite1), .out1(CpuWrite2), .in(CpuWritesToCache), .sel(MemAddressOut[0]));
  Multiplexer #(.enable("false")) multiplexer_1 (
    .in0(OldestWayDirtyBit1), .in1(OldestWayDirtyBit2), .out(isDirty), .sel(MemAddressOut[0]));
  Demultiplexer #(.enable("false")) demultiplexer_3 (
    .out0(UpdateAges1), .out1(UpdateAges2), .in(UpdateAges), .sel(MemAddressOut[0]));
  Multiplexer #(.enable("false"), .width(32)) multiplexer_2 (
    .in0(OldestWaySet1), .in1(OldestWaySet2), .out(InternalOldestWayToMem), .sel(MemAddressOut[0]));
  Multiplexer #(.enable("false"), .width(7)) multiplexer_3 (
    .in0(OldestTagSet1), .in1(OldestTagSet2), .out(InternalOldestTagToMem), .sel(MemAddressOut[0]));
  Multiplexer #(.enable("false"), .width(7)) multiplexer_4 (
    .in0(SavedCpuAddress), .in1(OldestTagToMem), .out(MemAddressOut[7:1]), .sel(MemWriteOut));
  NextStateFSM nextstatefsm_1 (
    .CurState(register_2_q), .CPURead(CpuReadIn), .CPUWrite(CpuWriteIn), .Contains(InternalContains),
    .isDirty(isDirty), .NextState(nextstatefsm_1_nextstate));
  Counter #(.max('h1), .ongoal("stay"), .width(1)) counter_1 (
    .clk(ClkIn), .D(PowerOn), .Q(counter_1_q));  // open: clr, load, up, count, carry
  Register #(.width(4)) register_2 (
    .D(nextstatefsm_1_nextstate), .en(1'b1), .clk(ClkIn), .Q(register_2_q));  // open: clr
  Set set_1 (
    .CpuTag(SavedCpuAddress), .CpuOff(offset_bits), .BlockPasssedIn(LineFromMemIn), .CpuReadIn(CpuReadIn),
    .CpuWriteIn(CpuWrite1), .PowerOnIn(PowerOnInternal), .CacheReadsFromMemoryIn(CachReadsFromMem1),
    .Clock(ClkIn), .ByteToWriteIn(CpuWriteValueIn), .UpdateAgesIn(UpdateAges1), .Contain(SetContains1),
    .ByteRead_Out(ByteReadSet1), .OldestWayToMemoryOut(OldestWaySet1), .OldestTagToMemoryOut(OldestTagSet1),
    .EvictedWayDirtyBit(OldestWayDirtyBit1));
  Set set_2 (
    .CpuTag(SavedCpuAddress), .CpuOff(offset_bits), .BlockPasssedIn(LineFromMemIn), .CpuReadIn(CpuReadIn),
    .CpuWriteIn(CpuWrite2), .PowerOnIn(PowerOnInternal), .CacheReadsFromMemoryIn(CachReadsFromMem2),
    .Clock(ClkIn), .ByteToWriteIn(CpuWriteValueIn), .UpdateAgesIn(UpdateAges2), .Contain(SetContains2),
    .ByteRead_Out(ByteReadSet2), .OldestWayToMemoryOut(OldestWaySet2), .OldestTagToMemoryOut(OldestTagSet2),
    .EvictedWayDirtyBit(OldestWayDirtyBit2));
  not not_1 (PowerOnInternal, counter_1_q);
  OutputFSM outputfsm_1 (
    .CurrState(register_2_q), .PowerOn(PowerOn), .ReadyOutput(ReadyOut),
    .CheckingIfCacheHasValue(CheckingIfCacheHasValue), .CPUReadsFromMemory(MemReadOut),
    .CPUWritesToCache(CpuWritesToCache), .WriteToMem(MemWriteOut), .UpdatingAges(UpdateAges));
  Multiplexer #(.enable("false"), .width(8)) multiplexer_5 (
    .in0(ByteReadSet1), .in1(ByteReadSet2), .out(ByteReadOut), .sel(MemAddressOut[0]));
  Multiplexer #(.enable("false")) multiplexer_6 (
    .in0(SetContains1), .in1(SetContains2), .out(InternalContains), .sel(MemAddressOut[0]));
  Register #(.width(1)) register_3 (
    .D(InternalContains), .en(CheckingIfCacheHasValue), .clk(ClkIn), .Q(DidContainOut));  // open: clr

  // Other names for the same wires on the sheet: clk = ClkIn; CpuAddress[9:0] = CpuAddressIn; CpuRead = CpuReadIn;
  //   CpuWrite = CpuWriteIn; CpuWriteValue[7:0] = CpuWriteValueIn; DidContain = DidContainOut;
  //   LineFromMem[31:0] = LineFromMemIn; MemAddress[7:0] = MemAddressOut;
  //   SavedCpuAddress[2:0] = {MemAddressOut[0], offset_bits}; set_bits = MemAddressOut[0];
  //   CachReadsFromMem = MemReadOut; MemRead = MemReadOut; Ready = ReadyOut; tag_bits[6:0] = SavedCpuAddress;
  //   ByteRead[7:0] = ByteReadOut; SelectedSetByteRead[7:0] = ByteReadOut; Line2Mem[31:0] = Line2MemOut;
  //   OldestWayToMem[31:0] = Line2MemOut; SelectedSetLine2Mem[31:0] = Line2MemOut; MemWrite = MemWriteOut;
  //   WritingToMem = MemWriteOut

  // Notes on the sheet:
  //   Saves CpuAddress until it's ready for the next address
  //   So cache knows to what Set it's reading the memory into
  //   So cache knows to what set to write into
  //   Cheks if the oldest way that is being evicted is dirty
  //   Updates Ages
  //   Writing out to memory
  //   Chooses between if we're writing to memory or reading from memory
  //   If the Cache is reading from memory then the MemAdderss we want to read from is made from  the tag bits that Cache is given from the CPU address and the set bits 
  //   If the Cache is writing to memory then the MemAdderss we want to read from is made from  the oldest way tag bits and the set bits 
endmodule

module Set (
  input  [6:0] CpuTag,
  input  [1:0] CpuOff,
  input  [31:0] BlockPasssedIn,
  input  CpuReadIn,
  input  CpuWriteIn,
  input  PowerOnIn,
  input  CacheReadsFromMemoryIn,
  input  Clock,
  input  [7:0] ByteToWriteIn,
  input  UpdateAgesIn,
  output Contain,
  output [7:0] ByteRead_Out,
  output [31:0] OldestWayToMemoryOut,
  output [6:0] OldestTagToMemoryOut,
  output EvictedWayDirtyBit
);

  wire and_4_out, CacheReadsFromMem0, CacheReadsFromMem1, CacheReadsFromMem2, CpuWrite0, CpuWrite1,
       CpuWrite2, DirtyBit0, DirtyBit1, DirtyBit2, Evict, not_1_out, not_2_out, not_3_out, not_4_out,
       or_2_out, ReadFromMem, Way0_Contain, Way1_Contain, Way2_Contain, WriteToMem;
  wire [1:0] Age0, Age1, Age2, AgeAccessed, OldestWayIndex, OldOrNewBits, WorkingWayIndex;
  wire [6:0] SavedTag0, SavedTag1, SavedTag2;
  wire [31:0] BlockFromMem, NewWayToWrite, OldestWayToMemoryOut_t, Return_Way0, Return_Way1, Return_Way2,
       WayToWorkWith;

  Demultiplexer #(.enable("false"), .select(2)) demultiplexer_1 (
    .out0(CpuWrite0), .out1(CpuWrite1), .out2(CpuWrite2), .in(CpuWriteIn), .sel(WorkingWayIndex));  // open: out3
  Multiplexer #(.enable("false"), .select(2), .width(2)) multiplexer_1 (
    .in0(Age0), .in1(Age1), .in2(Age2), .out(AgeAccessed), .sel(WorkingWayIndex));  // open: in3
  Multiplexer #(.enable("false"), .width(2)) multiplexer_2 (
    .in0(CpuOff), .in1(OldestWayIndex), .out(OldOrNewBits), .sel(CacheReadsFromMemoryIn));
  // Probe on AgeAccessed
  or or_1 (Contain, Way0_Contain, Way1_Contain, Way2_Contain);
  Demultiplexer #(.enable("false"), .select(2)) demultiplexer_2 (
    .out0(CacheReadsFromMem0), .out1(CacheReadsFromMem1), .out2(CacheReadsFromMem2),
    .in(CacheReadsFromMemoryIn), .sel(OldestWayIndex));  // open: out3
  not not_1 (not_1_out, EvictedWayDirtyBit);
  not not_2 (not_2_out, CacheReadsFromMemoryIn);
  and and_1 (ReadFromMem, not_2_out, Evict, not_1_out);
  WorkingWayInSet workingwayinset_1 (
    .Way0In(Way0_Contain), .Way1In(Way1_Contain), .Way2In(Way2_Contain), .ReturnWay0In(Return_Way0),
    .ReturnWay1In(Return_Way1), .ReturnWay2In(Return_Way2), .WorkingWayOut(WayToWorkWith),
    .WorkingWayIndex(WorkingWayIndex));
  Way way_1 (
    .CpuTag(CpuTag), .BlockPassedIn(BlockFromMem), .CpuWrite(CpuWrite0), .CpuRead(CpuReadIn),
    .InitalizedAgeIn(2'b00), .AccessedAgeIn(AgeAccessed), .PowerOnIn(PowerOnIn),
    .CacheReadsFromMemoryIn(CacheReadsFromMem0), .ClockIn(Clock), .UpdateAgesIn(UpdateAgesIn),
    .Contain(Way0_Contain), .ReturnWay(Return_Way0), .AgeAccessedOut(Age0), .SavedTagOut(SavedTag0),
    .SavedDirtyBitOut(DirtyBit0));
  Way way_2 (
    .CpuTag(CpuTag), .BlockPassedIn(BlockFromMem), .CpuWrite(CpuWrite1), .CpuRead(CpuReadIn),
    .InitalizedAgeIn(2'b01), .AccessedAgeIn(AgeAccessed), .PowerOnIn(PowerOnIn),
    .CacheReadsFromMemoryIn(CacheReadsFromMem1), .ClockIn(Clock), .UpdateAgesIn(UpdateAgesIn),
    .Contain(Way1_Contain), .ReturnWay(Return_Way1), .AgeAccessedOut(Age1), .SavedTagOut(SavedTag1),
    .SavedDirtyBitOut(DirtyBit1));
  Way way_3 (
    .CpuTag(CpuTag), .BlockPassedIn(BlockFromMem), .CpuWrite(CpuWrite2), .CpuRead(CpuReadIn),
    .InitalizedAgeIn(2'b10), .AccessedAgeIn(AgeAccessed), .PowerOnIn(PowerOnIn),
    .CacheReadsFromMemoryIn(CacheReadsFromMem2), .ClockIn(Clock), .UpdateAgesIn(UpdateAgesIn),
    .Contain(Way2_Contain), .ReturnWay(Return_Way2), .AgeAccessedOut(Age2), .SavedTagOut(SavedTag2),
    .SavedDirtyBitOut(DirtyBit2));
  ReadByte readbyte_1 (.WayReadIn(WayToWorkWith), .CpuOff(CpuOff), .ByteReturn(ByteRead_Out));
  or or_2 (or_2_out, CpuReadIn, CpuWriteIn);
  not not_3 (not_3_out, Contain);
  and and_2 (Evict, or_2_out, not_3_out);
  EvictOldest evictoldest_1 (
    .AgeIn0(Age0), .AgeIn1(Age1), .AgeIn2(Age2), .Way0In(Return_Way0), .Way1In(Return_Way1),
    .Way2In(Return_Way2), .DirtyBit0In(DirtyBit0), .DirtyBitIn1(DirtyBit1), .DirtyBitIn2(DirtyBit2),
    .OldestWayOut(OldestWayToMemoryOut_t), .OldestTagOut(OldestTagToMemoryOut), .OldestWay(OldestWayIndex),
    .OldestWayDirtyBit(EvictedWayDirtyBit));
  and and_3 (WriteToMem, Evict, EvictedWayDirtyBit);
  not not_4 (not_4_out, CacheReadsFromMemoryIn);
  and and_4 (and_4_out, CpuWriteIn, not_4_out);
  Multiplexer #(.enable("false"), .width(32)) multiplexer_3 (
    .in0(BlockPasssedIn), .in1(NewWayToWrite), .out(BlockFromMem), .sel(and_4_out));
  // Probe on OldestWayIndex
  BtyeWriteIn btyewritein_1 (
    .WayIn(WayToWorkWith), .ByteToReadIn(ByteToWriteIn), .CpuOff(CpuOff), .NewWayOut(NewWayToWrite));

  // Other names for the same wires on the sheet: BlockFromMemIn[31:0] = BlockPasssedIn;
  //   ByteToRead[7:0] = ByteRead_Out; ByteToReadOut[7:0] = ByteRead_Out; CacheReadsFromMem = CacheReadsFromMemoryIn;
  //   Clk = Clock; Contains_tag = Contain; CpuRead = CpuReadIn; CpuWrite = CpuWriteIn; off_bits[1:0] = CpuOff;
  //   OldestTagToMemory[6:0] = OldestTagToMemoryOut; OldestWayDirtyBit = EvictedWayDirtyBit;
  //   OldestWayToMemory[31:0] = OldestWayToMemoryOut; PowerOn = PowerOnIn; tag_bits[6:0] = CpuTag;
  //   UpdateAges = UpdateAgesIn

  // Notes on the sheet:
  //   we need to read from memory
  //   Let us know what way we are writing to
  //   Checks what Way the Cpu is working with
  //   If cache is reading from memory then it means that we are evicting oldest way so we are writing to the oldest ways index
  //   If any of the three ways in the set contain the tag
  //   If Cpu is reading from memory, then itt means that the Cpu kicked out that oldest way, so the cpu reads from memory into the oldest way
  //   If cpu writes or reads that means we are accessing a way and that way can either be the old way or the new off bits that are being passed in
  //   Chcks what way we're working with in the set
  //   If the cache is not reading from memory already and it's evicting the oldest way and the oldest way dirty bit is 0, then
  //   Reading from Cache
  //   Find out what btye to read from way that we're working with
  //   Return Byte if CPU wants to read and any of the 3 ways in set contains the desired tag bits
  //   If  you are reading to or writing from Memory and set doesn't contain tag then Evict equals 1
  //   Evicting Proccess
  //   Evicts Oldest Way In set
  //   If we are evicting way from cache and ways' dirty bit is one then we write the old way to memory
  //   WritingToCache
  //   Changing Way we are writing to
  //   If Cpu is writing into cache then it passes in the New way with the updated Btye that was requested to be written into the cache 
  //   If Cpu is not writing then it means that we are reading from memory, so we can just use the block that is being passed in
endmodule

module Way (
  input  [6:0] CpuTag,
  input  [31:0] BlockPassedIn,
  input  CpuWrite,
  input  CpuRead,
  input  [1:0] InitalizedAgeIn,
  input  [1:0] AccessedAgeIn,
  input  PowerOnIn,
  input  CacheReadsFromMemoryIn,
  input  ClockIn,
  input  UpdateAgesIn,
  output Contain,
  output [31:0] ReturnWay,
  output [1:0] AgeAccessedOut,
  output [6:0] SavedTagOut,
  output SavedDirtyBitOut
);

  wire and_1_out, and_2_out, BtyeWriteComplete, comparator_1_eq, or_1_out, or_2_out, or_3_out, or_4_out,
       Valid_Bit;
  wire [1:0] multiplexer_1_out, updateage_1_newage;

  and and_1 (and_1_out, CpuWrite, Contain);
  and and_2 (and_2_out, CpuWrite, Contain);
  or or_1 (or_1_out, CpuWrite, CacheReadsFromMemoryIn, PowerOnIn);
  or or_2 (or_2_out, CacheReadsFromMemoryIn, PowerOnIn);
  or or_3 (or_3_out, CacheReadsFromMemoryIn, and_1_out);
  Register #(.width(7)) SavedTag (
    .D(CpuTag), .en(CacheReadsFromMemoryIn), .clk(ClockIn), .Q(SavedTagOut));  // open: clr
  Register #(.width(1)) SavedValidBit (
    .D(CacheReadsFromMemoryIn), .en(or_2_out), .clk(ClockIn), .Q(Valid_Bit));  // open: clr
  Register #(.width(32)) SavedBlock (.D(BlockPassedIn), .en(or_3_out), .clk(ClockIn), .Q(ReturnWay));  // open: clr
  UpdateAge updateage_1 (.ThisWayAgeIn(AgeAccessedOut), .AccessedAgeIn(AccessedAgeIn), .newAge(updateage_1_newage));
  Register #(.width(1)) SavedDirtyBit (.D(and_2_out), .en(or_1_out), .clk(ClockIn), .Q(SavedDirtyBitOut));  // open: clr
  Multiplexer #(.enable("false"), .width(2)) multiplexer_1 (
    .in0(updateage_1_newage), .in1(InitalizedAgeIn), .out(multiplexer_1_out), .sel(PowerOnIn));
  or or_4 (or_4_out, PowerOnIn, UpdateAgesIn);
  // Probe on SavedDirtyBitOut
  // Probe on SavedTagOut
  // Probe on Valid_Bit
  Register #(.width(2)) SavedAge (
    .D(multiplexer_1_out), .en(or_4_out), .clk(ClockIn), .Q(AgeAccessedOut));  // open: clr
  // Probe on ReturnWay
  // Probe on AgeAccessedOut
  Comparator #(.width(7)) comparator_1 (.a(CpuTag), .b(SavedTagOut), .eq(comparator_1_eq));  // open: gt, lt
  and and_3 (BtyeWriteComplete, SavedDirtyBitOut, CpuWrite);
  and and_4 (Contain, comparator_1_eq, Valid_Bit);

  // Other names for the same wires on the sheet: AccessedAge[1:0] = AccessedAgeIn; Block_in[31:0] = BlockPassedIn;
  //   CacheReadsFromMemory = CacheReadsFromMemoryIn; Clk = ClockIn; Contains_tag = Contain;
  //   CpuReadsFromCache = CpuRead; CpuWritesToCache = CpuWrite; InitalizedAge[1:0] = InitalizedAgeIn;
  //   PowerOn = PowerOnIn; Saved_block[31:0] = ReturnWay; Saved_tag_bits[6:0] = SavedTagOut;
  //   SavedAgeForWay[1:0] = AgeAccessedOut; SavedDirtyBitForWay = SavedDirtyBitOut; tag_bits[6:0] = CpuTag;
  //   UpdateAges = UpdateAgesIn

  // Notes on the sheet:
  //   FSM
  //   FSM
  //   FSM
  //   FSM
  //   FSM
  //   Checks if Caches' saved Tag Bits matches the Tag Bits passed in
  //   Write to cache is complete if dirty bit is 1 and the cpu is writing to cache
  //   FSM
endmodule

module WorkingWayInSet (
  input  Way0In,
  input  Way1In,
  input  Way2In,
  input  [31:0] ReturnWay0In,
  input  [31:0] ReturnWay1In,
  input  [31:0] ReturnWay2In,
  output [31:0] WorkingWayOut,
  output [1:0] WorkingWayIndex
);

  BitFinder #(.width(3)) bitfinder_1 (.in({Way2In, Way1In, Way0In}), .index(WorkingWayIndex));  // open: found
  Multiplexer #(.enable("false"), .select(2), .width(32)) multiplexer_1 (
    .in0(ReturnWay0In), .in1(ReturnWay1In), .in2(ReturnWay2In), .out(WorkingWayOut), .sel(WorkingWayIndex));  // open: in3
  // Probe on WorkingWayIndex

  // Other names for the same wires on the sheet: Way0 = Way0In; Way1 = Way1In; Way2 = Way2In;
  //   Return_Working_Way[31:0] = WorkingWayOut; ReturnWay0[31:0] = ReturnWay0In; ReturnWay1[31:0] = ReturnWay1In;
  //   ReturnWay2[31:0] = ReturnWay2In; Working_Way[1:0] = WorkingWayIndex
endmodule

module ReadByte (
  input  [31:0] WayReadIn,
  input  [1:0] CpuOff,
  output [7:0] ByteReturn
);

  wire [1:0] ChooseBtye;
  wire [3:0] comparator_4_eq;

  Comparator #(.width(2)) comparator_1 (.a(WayReadIn[25:24]), .b(CpuOff), .eq(comparator_4_eq[3]));  // open: gt, lt
  Comparator #(.width(2)) comparator_2 (.a(WayReadIn[17:16]), .b(CpuOff), .eq(comparator_4_eq[2]));  // open: gt, lt
  Comparator #(.width(2)) comparator_3 (.a(WayReadIn[9:8]), .b(CpuOff), .eq(comparator_4_eq[1]));  // open: gt, lt
  Comparator #(.width(2)) comparator_4 (.a(WayReadIn[1:0]), .b(CpuOff), .eq(comparator_4_eq[0]));  // open: gt, lt
  // Probe on ChooseBtye
  BitFinder #(.width(4)) bitfinder_1 (.in(comparator_4_eq), .index(ChooseBtye));  // open: found
  Multiplexer #(.enable("false"), .select(2), .width(8)) multiplexer_1 (
    .in0(WayReadIn[7:0]), .in1(WayReadIn[15:8]), .in2(WayReadIn[23:16]), .in3(WayReadIn[31:24]),
    .out(ByteReturn), .sel(ChooseBtye));
  // Probe on ByteReturn

  // Other names for the same wires on the sheet: ByteReturnInBlock[7:0] = ByteReturn; off_bits[1:0] = CpuOff;
  //   Byte0[7:0] = WayReadIn[7:0]; Way[31:0] = WayReadIn; Byte1[7:0] = WayReadIn[15:8]; Byte2[7:0] = WayReadIn[23:16];
  //   Byte3[7:0] = WayReadIn[31:24]
endmodule

module UpdateAge (
  input  [1:0] ThisWayAgeIn,
  input  [1:0] AccessedAgeIn,
  output [1:0] newAge
);

  wire Equal, GreaterThan, LessThan;
  wire [1:0] adder_1_out;

  Adder #(.width(2)) adder_1 (.a(ThisWayAgeIn), .b(2'b01), .out(adder_1_out));  // open: cin, cout
  Comparator #(.mode("unsigned"), .width(2)) comparator_1 (
    .a(ThisWayAgeIn), .b(AccessedAgeIn), .gt(GreaterThan), .eq(Equal), .lt(LessThan));
  Multiplexer #(.enable("false"), .width(2)) multiplexer_1 (
    .in1(adder_1_out), .out(newAge), .sel(LessThan));  // open: in0
  Multiplexer #(.enable("false"), .width(2)) multiplexer_2 (
    .in1(ThisWayAgeIn), .out(newAge), .sel(GreaterThan));  // open: in0
  Multiplexer #(.enable("false"), .width(2)) multiplexer_3 (.in1(2'b00), .out(newAge), .sel(Equal));  // open: in0
  // Probe on newAge
  // Probe on newAge
  // Probe on newAge

  // Other names for the same wires on the sheet: AccessedAge[1:0] = AccessedAgeIn; UpdatingAge[1:0] = newAge;
  //   WayAge[1:0] = ThisWayAgeIn

  // Notes on the sheet:
  //   Age of this way is less than Age Accessed 
  //   Age of this way is less than Age Accessed 
  //   Age of this way is equa to Age Accessed 
endmodule

module GetOldestWay (
  input  [1:0] AgeIn0,
  input  [1:0] AgeIn1,
  input  [1:0] AgeIn2,
  output [1:0] OldestWayOut
);

  wire [2:0] comparator_3_eq;

  Comparator #(.mode("unsigned"), .width(2)) comparator_1 (
    .a(AgeIn2), .b(2'b10), .eq(comparator_3_eq[2]));  // open: gt, lt
  Comparator #(.mode("unsigned"), .width(2)) comparator_2 (
    .a(AgeIn1), .b(2'b10), .eq(comparator_3_eq[1]));  // open: gt, lt
  Comparator #(.mode("unsigned"), .width(2)) comparator_3 (
    .a(AgeIn0), .b(2'b10), .eq(comparator_3_eq[0]));  // open: gt, lt
  BitFinder #(.width(3)) bitfinder_1 (.in(comparator_3_eq), .index(OldestWayOut));  // open: found

  // Other names for the same wires on the sheet: Age0[1:0] = AgeIn0; Age1[1:0] = AgeIn1; Age2[1:0] = AgeIn2;
  //   OldestWay[1:0] = OldestWayOut

  // Notes on the sheet:
  //   Compares each age to see which one is equal to 2 . If equal to 2 then it's the oldest age
endmodule

module EvictOldest (
  input  [1:0] AgeIn0,
  input  [1:0] AgeIn1,
  input  [1:0] AgeIn2,
  input  [31:0] Way0In,
  input  [31:0] Way1In,
  input  [31:0] Way2In,
  input  DirtyBit0In,
  input  DirtyBitIn1,
  input  DirtyBitIn2,
  output [31:0] OldestWayOut,
  output [6:0] OldestTagOut,
  output [1:0] OldestWay,
  output OldestWayDirtyBit
);

  wire [6:0] SavedTag0, SavedTag1, SavedTag2;

  Multiplexer #(.enable("false"), .select(2), .width(32)) multiplexer_1 (
    .in0(Way0In), .in1(Way1In), .in2(Way2In), .out(OldestWayOut), .sel(OldestWay));  // open: in3
  Multiplexer #(.enable("false"), .select(2)) multiplexer_2 (
    .in0(DirtyBit0In), .in1(DirtyBitIn1), .in2(DirtyBitIn2), .out(OldestWayDirtyBit), .sel(OldestWay));  // open: in3
  Multiplexer #(.enable("false"), .select(2), .width(7)) multiplexer_3 (
    .in0(SavedTag0), .in1(SavedTag1), .in2(SavedTag2), .out(OldestTagOut), .sel(OldestWay));  // open: in3
  GetOldestWay getoldestway_1 (.AgeIn0(AgeIn0), .AgeIn1(AgeIn1), .AgeIn2(AgeIn2), .OldestWayOut(OldestWay));

  // Other names for the same wires on the sheet: Age0[1:0] = AgeIn0; Age1[1:0] = AgeIn1; Age2[1:0] = AgeIn2;
  //   DirtyBit0 = DirtyBit0In; DirtyBit1 = DirtyBitIn1; DirtyBit2 = DirtyBitIn2; DirtyBitIsOne = OldestWayDirtyBit;
  //   OldestTagToMemory[6:0] = OldestTagOut; OldestWayIndex[1:0] = OldestWay; OldestWayToMemory[31:0] = OldestWayOut;
  //   Way0[31:0] = Way0In; Way1[31:0] = Way1In; Way2[31:0] = Way2In

  // Notes on the sheet:
  //   Gets oldest way
  //   Chooses Oldest way
  //   Chooes Oldest Way Dirty Bit
  //   Chooses Oldest Way Tag
endmodule

module BtyeWriteIn (
  input  [31:0] WayIn,
  input  [7:0] ByteToReadIn,
  input  [1:0] CpuOff,
  output [31:0] NewWayOut
);

  wire [1:0] ChooseBtyeToChange;
  wire [3:0] comparator_4_eq;
  wire [7:0] Byte0New, Byte1New, Byte2New, Byte3New;

  Demultiplexer #(.enable("false"), .select(2), .width(8)) demultiplexer_1 (
    .out0(Byte0New), .out1(Byte1New), .out2(Byte2New), .out3(Byte3New), .in(ByteToReadIn),
    .sel(ChooseBtyeToChange));
  Comparator #(.width(2)) comparator_1 (.a(WayIn[25:24]), .b(CpuOff), .eq(comparator_4_eq[3]));  // open: gt, lt
  Comparator #(.width(2)) comparator_2 (.a(WayIn[17:16]), .b(CpuOff), .eq(comparator_4_eq[2]));  // open: gt, lt
  Comparator #(.width(2)) comparator_3 (.a(WayIn[9:8]), .b(CpuOff), .eq(comparator_4_eq[1]));  // open: gt, lt
  Comparator #(.width(2)) comparator_4 (.a(WayIn[1:0]), .b(CpuOff), .eq(comparator_4_eq[0]));  // open: gt, lt
  Multiplexer #(.enable("false"), .select(2), .width(32)) multiplexer_1 (
    .in0({WayIn[31:8], Byte0New}), .in1({WayIn[31:16], Byte1New, WayIn[7:0]}),
    .in2({WayIn[31:24], Byte2New, WayIn[15:0]}), .in3({Byte3New, WayIn[23:0]}), .out(NewWayOut),
    .sel(ChooseBtyeToChange));
  BitFinder #(.width(4)) bitfinder_1 (.in(comparator_4_eq), .index(ChooseBtyeToChange));  // open: found
  // Probe on ChooseBtyeToChange

  // Other names for the same wires on the sheet: ByteToWriteInTest[7:0] = ByteToReadIn;
  //   NewWay0[31:0] = {WayIn[31:8], Byte0New}; NewWay1[31:0] = {WayIn[31:16], Byte1New, WayIn[7:0]};
  //   NewWay2[31:0] = {WayIn[31:24], Byte2New, WayIn[15:0]}; Byte3[7:0] = WayIn[31:24]; Way[31:0] = WayIn;
  //   Byte0[7:0] = WayIn[7:0]; NewWay3[31:0] = {Byte3New, WayIn[23:0]}; Byte1[7:0] = WayIn[15:8];
  //   Byte2[7:0] = WayIn[23:16]; NewWayWrittenTo[31:0] = NewWayOut; off_bits[1:0] = CpuOff
endmodule

module NextStateFSM (
  input  [3:0] CurState,
  input  CPURead,
  input  CPUWrite,
  input  Contains,
  input  isDirty,
  output [3:0] NextState
);

  wire and_1_out, and_2_out, and_3_out, and_4_out, and_5_out, and_6_out, and_7_out, and_8_out, and_9_out,
       and_10_out, and_11_out, and_12_out, and_13_out, and_14_out, and_15_out, and_16_out, and_17_out,
       not_1_out, not_2_out, not_3_out, not_4_out, not_5_out, not_6_out;

  not not_1 (not_1_out, CurState[3]);
  not not_2 (not_2_out, CurState[2]);
  not not_3 (not_3_out, CurState[1]);
  not not_4 (not_4_out, CurState[0]);
  not not_5 (not_5_out, Contains);
  not not_6 (not_6_out, isDirty);
  and and_1 (and_1_out, CurState[1], CurState[0], not_6_out);
  and and_2 (and_2_out, not_1_out, CurState[2], not_3_out, not_4_out);
  and and_3 (and_3_out, CurState[2], CurState[1], CurState[0]);
  and and_4 (and_4_out, CurState[3], CurState[0]);
  and and_5 (and_5_out, CurState[3], CurState[1]);
  and and_6 (and_6_out, CurState[3], CurState[2], Contains);
  and and_7 (and_7_out, not_1_out, not_3_out);
  and and_8 (and_8_out, not_2_out, not_3_out, not_4_out, CPUWrite);
  and and_9 (and_9_out, not_1_out, CurState[0]);
  and and_10 (and_10_out, CurState[2], CurState[1]);
  and and_11 (and_11_out, CurState[1], not_4_out);
  and and_12 (and_12_out, not_2_out, CurState[1], isDirty);
  and and_13 (and_13_out, CurState[3], CurState[1]);
  and and_14 (and_14_out, CurState[3], CurState[2], not_4_out, not_5_out);
  and and_15 (and_15_out, CurState[1], CurState[0]);
  and and_16 (and_16_out, CurState[3], not_2_out, not_3_out);
  and and_17 (and_17_out, CurState[3], not_3_out, not_4_out, not_5_out);
  or or_1 (NextState[2], and_7_out, and_8_out, and_9_out, and_10_out);
  or or_2 (NextState[1], and_11_out, and_12_out, and_13_out, and_14_out);
  or or_3 (NextState[0], and_15_out, and_16_out, and_17_out);
  or or_4 (NextState[3], and_1_out, and_2_out, and_3_out, and_4_out, and_5_out, and_6_out);
endmodule

module OutputFSM (
  input  [3:0] CurrState,
  output PowerOn,
  output ReadyOutput,
  output CheckingIfCacheHasValue,
  output CPUReadsFromMemory,
  output CPUWritesToCache,
  output WriteToMem,
  output UpdatingAges
);

  wire and_2_out, and_3_out, not_1_out, not_2_out, not_3_out, not_4_out;

  not not_1 (not_1_out, CurrState[3]);
  not not_2 (not_2_out, CurrState[2]);
  not not_3 (not_3_out, CurrState[1]);
  not not_4 (not_4_out, CurrState[0]);
  and and_1 (PowerOn, not_2_out, not_3_out, not_4_out);
  and and_2 (and_2_out, not_1_out, not_2_out, not_3_out, CurrState[0]);
  or or_1 (ReadyOutput, and_2_out, and_3_out);
  and and_3 (and_3_out, not_1_out, CurrState[2], not_3_out, not_4_out);
  and and_4 (CheckingIfCacheHasValue, CurrState[3], CurrState[2], not_3_out, not_4_out);
  and and_5 (CPUReadsFromMemory, CurrState[3], CurrState[2], not_3_out, CurrState[0]);
  and and_6 (CPUWritesToCache, not_1_out, CurrState[2], not_3_out, CurrState[0]);
  and and_7 (WriteToMem, not_1_out, CurrState[2], CurrState[1], CurrState[0]);
  and and_8 (UpdatingAges, CurrState[3], not_2_out, not_3_out, not_4_out);
endmodule
